# Fritzing sketch nano_wiring (saved by Fritzing 0.9.3b)
breadboards: 1

parts:
  GY2 = MPU-6050 Board GY-521 [form="♀ (female)" package=THT]
  8x8_LED_Modul_mit_MAX2 = 8x8 LED Modul mit MAX7219 [package=THT]
  R2 = Resistor [tolerance=±5% resistance=10 package="2010 [SMD]"]
  J2 = Piezo Speaker
  S2 = Round Pushbutton
  Part4 = Arduino Nano (Rev3.0) (ICSP)

nets:
  N1: GY2.pin1, Part4.3V3
  N2: GY2.pin2, 8x8_LED_Modul_mit_MAX2.GND_Eingang, R2.Pin_1, S2.leg0, Part4.GND
  N3: GY2.pin3, Part4.A5
  N4: GY2.pin4, Part4.A4
  N5: GY2.pin8, Part4.D2
  N6: 8x8_LED_Modul_mit_MAX2.VCC_Eingang, Part4.5V
  N7: 8x8_LED_Modul_mit_MAX2.DIN_Eingang, Part4.D11/MOSI
  N8: 8x8_LED_Modul_mit_MAX2.CS_Eingang, Part4.D10
  N9: 8x8_LED_Modul_mit_MAX2.CLK_Eingang, Part4.D13/SCK
  N10: R2.Pin_0, J2.pin2
  N11: J2.pin1, Part4.D8
  N12: S2.leg1, Part4.D3

custom parts:
  MPU-6050 Board GY-521: Acelerometro y Giroscopio MPU-6050 Board GY-521
