# Fritzing sketch nano_wiring_holed_pcb (saved by Fritzing 0.9.3b)
perfboards: 1

parts:
  8x8_LED_Modul_mit_MAX4 = 8x8 LED Modul mit MAX7219 [package=THT]
  GY4 = MPU-6050 Board GY-521 [form="♀ (female)" package=THT]
  Part7 = Arduino Nano (Rev3.0)
  VCC2 = Battery block 9V
  S5 = Round Pushbutton
  J5 = Piezo Speaker
  R6 = Resistor [tolerance=±5% resistance=10 package="2010 [SMD]"]
  C1 = Ceramic Capacitor [capacitance="100 nF" package="0603 [SMD, multilayer]"]
  R7 = Resistor [tolerance=±5% resistance=10k package="1206 [SMD]"]
  R8 = Resistor [tolerance=±5% resistance=10k package="1206 [SMD]"]

nets:
  N1: 8x8_LED_Modul_mit_MAX4.VCC_Eingang, Part7.5V
  N2: 8x8_LED_Modul_mit_MAX4.GND_Eingang, GY4.pin2, Part7.GND, VCC2.-, S5.leg0, J5.pin2, C1.1, R8.Pin_1
  N3: 8x8_LED_Modul_mit_MAX4.DIN_Eingang, Part7.D11/MOSI
  N4: 8x8_LED_Modul_mit_MAX4.CS_Eingang, Part7.D10
  N5: 8x8_LED_Modul_mit_MAX4.CLK_Eingang, Part7.D13/SCK
  N6: GY4.pin1, Part7.3V3
  N7: GY4.pin3, Part7.A5
  N8: GY4.pin4, Part7.A4
  N9: GY4.pin8, Part7.D2
  N10: Part7.D3, S5.leg1
  N11: Part7.D8, R6.Pin_1
  N12: Part7.VIN, R7.Pin_0
  N13: Part7.A1, C1.0
  N14: J5.pin1, R6.Pin_0
  N15: R7.Pin_1, R8.Pin_0

custom parts:
  MPU-6050 Board GY-521: Acelerometro y Giroscopio MPU-6050 Board GY-521
